# Fritzing sketch submarine (saved by Fritzing 0.9.2b)
breadboards: 1

parts:
  Left_plane = Basic Servo  # not connected
  Rudder_bottom = Basic Servo  # not connected
  Right_plane = Basic Servo  # not connected
  Board_source = DC Power [voltage=5V]
  Propulsion_source = DC Power [voltage=6V]  # not connected
  Servomotors_source = DC Power [voltage=6V]  # not connected
  U1 = L9110 H-bridge module [part_number="L9110 H-bridge"]
  Part5 = IR Receiver Breakout [package=PCB]  # not connected
  BAT1 = Battery Holders [package=battery-aa]
  Rudder_top = Basic Servo  # not connected
  U2 = HIH-4030 [package=hih-4030]  # not connected
  Part1 = Arduino Nano (Rev3.0)
  Ballast = DC Motor
  Propeller = DC Motor with two-phase hall-encoder

nets:
  N1: Board_source.V+, Part1.VIN
  N2: Board_source.V-, Part1.GND
  N3: U1.GND, BAT1.-
  N4: U1.VCC, BAT1.+
  N5: U1.MOTOR_A-A, Ballast.pin_1
  N6: U1.MOTOR_A-B, Ballast.pin_2
  N7: U1.MOTOR_B-A, Propeller.pin1
  N8: U1.MOTOR_B-B, Propeller.pin6
